# Fritzing sketch mkr100withinputs (saved by Fritzing 0.9.3b)
perfboards: 3

parts:
  J1 = male pin header, 2 pins [form="♂ (male)"]
  J2 = male pin header, 2 pins [form="♂ (male)"]
  J3 = male pin header, 4 pins [form="♂ (male)"]
  Part1 = Arduino MKR1000
  J4 = female pin header, 14 pins [form="♀ (female)"]  # not connected
  J5 = female pin header, 14 pins [form="♀ (female)"]
  J6 = female pin header, 4 pins [form="♀ (female)"]
  J7 = male pin header, 2 pins [form="♂ (male)"]  # not connected
  R1 = Resistor [tolerance=±5% resistance=10k package=THT]
  R2 = Resistor [tolerance=±5% resistance=10k package=THT]
  J8 = female pin header, 14 pins [form="♀ (female)"]
  J9 = female pin header, 14 pins [form="♀ (female)"]
  R3 = Resistor [tolerance=±5% resistance=10k package=THT]
  R4 = Resistor [tolerance=±5% resistance=10k package=THT]
  J10 = female pin header, 4 pins [form="♀ (female)"]
  J11 = male pin header, 2 pins [form="♂ (male)"]

nets:
  N1: J1.pin1, J3.pin1
  N2: J1.pin2, J3.pin2
  N3: J2.pin1, J3.pin4
  N4: J2.pin2, J3.pin3
  N5: Part1.AREF, J8.pin14
  N6: Part1.A0_DAC0, J8.pin13
  N7: Part1.A1, J8.pin12
  N8: Part1.A2, J8.pin11
  N9: Part1.A3, J8.pin10
  N10: Part1.A4, J8.pin9
  N11: Part1.A5, J8.pin8
  N12: Part1.A6, J8.pin7
  N13: Part1.D0, J8.pin6
  N14: Part1.D1, J8.pin5
  N15: Part1.D2_PWM, J8.pin4
  N16: Part1.D3_PWM, J8.pin3
  N17: Part1.D4_PWM, J8.pin2
  N18: Part1.D5_PWM, J8.pin1
  N19: Part1.D6, J9.pin1, R3.Pin_1, J10.pin4
  N20: Part1.D7, J9.pin2, R4.Pin_1, J10.pin1
  N21: Part1.D8_MOSI, J9.pin3
  N22: Part1.D9_SCK, J9.pin4
  N23: Part1.D10_MISO, J9.pin5
  N24: Part1.D11_SDA, J9.pin6
  N25: Part1.D12_SCL, J9.pin7
  N26: Part1.D13_RX, J9.pin8, J11.pin2
  N27: Part1.14_TX, J9.pin9, J11.pin1
  N28: Part1.RESET, J9.pin10
  N29: Part1.GND, J9.pin11, R3.Pin_0, R4.Pin_0
  N30: Part1.VCC, J9.pin12
  N31: Part1.VIN, J9.pin13
  N32: Part1.5V, J9.pin14, J10.pin2, J10.pin3
  N33: J5.pin1, J6.pin1, R1.Pin_0
  N34: J5.pin2, J6.pin4, R2.Pin_0
  N35: J5.pin11, R2.Pin_1
  N36: J5.pin14, J6.pin3

custom parts:
  Arduino MKR1000: MKR1000 is a powerful board that combines the functionality of the Zero and the Wi-Fi Shield. It is the ideal solution for makers wanting to design IoT projects with minimal previous experience in networking
